// Logisim project processador8bits.circ as structural Verilog: 11 circuits, main circuit main
module main (
  input  B7,
  input  in_2,
  input  A7,
  input  in_4,
  input  B6,
  input  in_6,
  input  A6,
  input  in_8,
  input  B5,
  input  in_10,
  input  A5,
  input  in_12,
  input  B4,
  input  in_14,
  input  A4,
  input  in_16,
  input  B3,
  input  in_18,
  input  A3,
  input  in_20,
  input  B2,
  input  in_22,
  input  A2,
  input  in_24,
  input  B1,
  input  in_26,
  input  A1,
  input  in_28,
  input  B0,
  input  in_30,
  input  A0,
  input  in_32,
  input  BC7,
  input  BC6,
  input  BC5,
  input  BC4,
  input  BC3,
  input  BC2,
  input  BC1,
  input  BC0,
  input  AC7,
  input  AC6,
  input  AC5,
  input  AC4,
  input  AC3,
  input  AC2,
  input  AC1,
  input  AC0,
  output cout,
  output out_50,
  output C7,
  output out_52,
  output C6,
  output out_54,
  output C5,
  output out_56,
  output C4,
  output out_58,
  output C3,
  output out_60,
  output C2,
  output out_62,
  output C1,
  output out_64,
  output C0,
  output out_66,
  output BT,
  output LW,
  output EQ
);

  somador8bits somador8bits_1 (
    .B7(B7), .A7(A7), .B6(B6), .A6(A6), .B5(B5), .A5(A5), .B4(B4), .A4(A4), .B3(B3), .A3(A3), .B2(B2),
    .A2(A2), .B1(B1), .A1(A1), .B0(B0), .A0(A0), .cout(cout), .C7(C7), .C6(C6), .C5(C5), .C4(C4), .C3(C3),
    .C2(C2), .C1(C1), .C0(C0));
  comparador8bits comparador8bits_1 (
    .B7(BC7), .B6(BC6), .B5(BC5), .B4(BC4), .B3(BC3), .B2(BC2), .B1(BC1), .B0(BC0), .A7(AC7), .A6(AC6),
    .A5(AC5), .A4(AC4), .A3(AC3), .A2(AC2), .A1(AC1), .A0(AC0), .BT(BT), .LW(LW), .EQ(EQ));
  subtrator8bits subtrator8bits_1 (
    .B7(in_2), .B6(in_4), .B5(in_6), .B4(in_8), .B3(in_10), .B2(in_12), .B1(in_14), .B0(in_16), .A7(in_18),
    .A6(in_20), .A5(in_22), .A4(in_24), .A3(in_26), .A2(in_28), .A1(in_30), .A0(in_32), .cout(out_50),
    .C7(out_52), .C6(out_54), .C5(out_56), .C4(out_58), .C3(out_60), .C2(out_62), .C1(out_64), .C0(out_66));
endmodule

module somador (
  input  A,
  input  B,
  input  CARRY,
  output s,
  output cout
);

  wire and_1_out, and_2_out, and_3_out, xor_1_out;

  xor xor_1 (xor_1_out, A, B);
  and and_1 (and_1_out, A, B);
  and and_2 (and_2_out, A, CARRY);
  and and_3 (and_3_out, B, CARRY);
  xor xor_2 (s, xor_1_out, CARRY);
  or or_1 (cout, and_1_out, and_2_out, and_3_out);
endmodule

module somador4bits (
  input  CARRY,
  input  B3,
  input  A3,
  input  B2,
  input  A2,
  input  B1,
  input  A1,
  input  B0,
  input  A0,
  output C3,
  output C2,
  output C1,
  output C0,
  output cout
);

  wire somador_2_cout, somador_3_cout, somador_4_cout;

  somador somador_1 (.A(A3), .B(B3), .CARRY(somador_2_cout), .s(C3), .cout(cout));
  somador somador_2 (.A(A2), .B(B2), .CARRY(somador_3_cout), .s(C2), .cout(somador_2_cout));
  somador somador_3 (.A(A1), .B(B1), .CARRY(somador_4_cout), .s(C1), .cout(somador_3_cout));
  somador somador_4 (.A(A0), .B(B0), .CARRY(CARRY), .s(C0), .cout(somador_4_cout));
endmodule

module somador8bits (
  input  B7,
  input  A7,
  input  B6,
  input  A6,
  input  B5,
  input  A5,
  input  B4,
  input  A4,
  input  B3,
  input  A3,
  input  B2,
  input  A2,
  input  B1,
  input  A1,
  input  B0,
  input  A0,
  output cout,
  output C7,
  output C6,
  output C5,
  output C4,
  output C3,
  output C2,
  output C1,
  output C0
);

  wire somador4bits_2_cout;

  somador4bits somador4bits_1 (
    .CARRY(somador4bits_2_cout), .B3(B7), .A3(A7), .B2(B6), .A2(A6), .B1(B5), .A1(A5), .B0(B4), .A0(A4),
    .C3(C7), .C2(C6), .C1(C5), .C0(C4), .cout(cout));
  somador4bits somador4bits_2 (
    .CARRY(1'b0), .B3(B3), .A3(A3), .B2(B2), .A2(A2), .B1(B1), .A1(A1), .B0(B0), .A0(A0), .C3(C3), .C2(C2),
    .C1(C1), .C0(C0), .cout(somador4bits_2_cout));
endmodule

module subtrator8bits (
  input  B7,
  input  B6,
  input  B5,
  input  B4,
  input  B3,
  input  B2,
  input  B1,
  input  B0,
  input  A7,
  input  A6,
  input  A5,
  input  A4,
  input  A3,
  input  A2,
  input  A1,
  input  A0,
  output cout,
  output C7,
  output C6,
  output C5,
  output C4,
  output C3,
  output C2,
  output C1,
  output C0
);

  wire not_1_out, not_2_out, not_3_out, not_4_out, not_5_out, not_6_out, not_7_out, not_8_out,
       somador8bits_1_c0, somador8bits_1_c1, somador8bits_1_c2, somador8bits_1_c3, somador8bits_1_c4,
       somador8bits_1_c5, somador8bits_1_c6, somador8bits_1_c7, somador8bits_1_cout;

  not not_1 (not_1_out, A7);
  not not_2 (not_2_out, A6);
  not not_3 (not_3_out, A5);
  not not_4 (not_4_out, A4);
  not not_5 (not_5_out, A3);
  not not_6 (not_6_out, A2);
  not not_7 (not_7_out, A1);
  not not_8 (not_8_out, A0);
  somador8bits somador8bits_1 (
    .B7(1'b0), .A7(not_1_out), .B6(1'b0), .A6(not_2_out), .B5(1'b0), .A5(not_3_out), .B4(1'b0),
    .A4(not_4_out), .B3(1'b0), .A3(not_5_out), .B2(1'b0), .A2(not_6_out), .B1(1'b0), .A1(not_7_out),
    .B0(1'b1), .A0(not_8_out), .cout(somador8bits_1_cout), .C7(somador8bits_1_c7), .C6(somador8bits_1_c6),
    .C5(somador8bits_1_c5), .C4(somador8bits_1_c4), .C3(somador8bits_1_c3), .C2(somador8bits_1_c2),
    .C1(somador8bits_1_c1), .C0(somador8bits_1_c0));
  somador8bits somador8bits_2 (
    .B7(B7), .A7(somador8bits_1_c7), .B6(B6), .A6(somador8bits_1_c6), .B5(B5), .A5(somador8bits_1_c5),
    .B4(B4), .A4(somador8bits_1_c4), .B3(B3), .A3(somador8bits_1_c3), .B2(B2), .A2(somador8bits_1_c2),
    .B1(B1), .A1(somador8bits_1_c1), .B0(B0), .A0(somador8bits_1_c0), .cout(cout), .C7(C7), .C6(C6), .C5(C5),
    .C4(C4), .C3(C3), .C2(C2), .C1(C1), .C0(C0));
  // also tied to GND on the sheet: somador8bits_1_cout
endmodule

module comparador8bits_test (
  input  B7,
  input  A7,
  input  B6,
  input  A6,
  output better,
  output lower,
  output equal
);

  wire and_1_out, and_2_out, and_3_out, and_4_out, and_5_out, and_6_out, and_7_out, and_8_out, and_9_out,
       and_10_out, or_1_out, or_2_out, xor_1_out, xor_2_out, xor_3_out, xor_4_out;

  xor xor_1 (xor_1_out, B7, A7);
  and and_1 (and_1_out, B7, A7);
  and and_2 (and_2_out, B6, A6);
  and and_3 (and_3_out, and_1_out, B6);
  and and_4 (and_4_out, and_1_out, A6);
  and and_5 (and_5_out, and_2_out, 1'b0);
  and and_6 (and_6_out, and_2_out, 1'b0);
  and and_7 (and_7_out, B7, xor_1_out);
  and and_8 (and_8_out, A7, xor_1_out);
  or or_1 (or_1_out, and_3_out, and_4_out);
  or or_2 (or_2_out, and_5_out, and_6_out);
  xor xor_2 (xor_2_out, and_1_out, or_1_out);
  xor xor_3 (xor_3_out, B6, A6);
  xor xor_4 (xor_4_out, and_2_out, or_2_out);
  and and_9 (and_9_out, B6, xor_3_out);
  and and_10 (and_10_out, xor_3_out, A6);
  or or_3 (better, and_7_out, and_9_out);
  or or_4 (lower, and_8_out, and_10_out);
  or or_5 (equal, xor_2_out, xor_4_out);
endmodule

module comparador1bit (
  input  B0,
  input  A0,
  input  r_BT,
  input  r_LW,
  input  r_EQ,
  output BT,
  output LW,
  output EQ
);

  wire and_1_out, and_2_out, and_3_out, and_4_out, and_5_out, and_6_out, and_7_out, not_1_out, not_2_out,
       not_3_out, not_4_out, not_5_out, not_6_out, xor_1_out;

  xor xor_1 (xor_1_out, B0, A0);
  and and_1 (and_1_out, B0, A0);
  and and_2 (and_2_out, B0, xor_1_out);
  and and_3 (and_3_out, A0, xor_1_out);
  not not_1 (not_1_out, r_LW);
  not not_2 (not_2_out, r_BT);
  and and_4 (and_4_out, and_2_out, not_1_out);
  and and_5 (and_5_out, and_3_out, not_2_out);
  or or_1 (BT, and_4_out, r_BT);
  or or_2 (LW, and_5_out, r_LW);
  not not_3 (not_3_out, r_BT);
  not not_4 (not_4_out, r_LW);
  and and_6 (and_6_out, and_1_out, not_3_out, not_4_out);
  not not_5 (not_5_out, B0);
  not not_6 (not_6_out, A0);
  and and_7 (and_7_out, not_5_out, not_6_out, r_EQ);
  or or_3 (EQ, and_6_out, and_7_out);
endmodule

module comparador8bits (
  input  B7,
  input  B6,
  input  B5,
  input  B4,
  input  B3,
  input  B2,
  input  B1,
  input  B0,
  input  A7,
  input  A6,
  input  A5,
  input  A4,
  input  A3,
  input  A2,
  input  A1,
  input  A0,
  output BT,
  output LW,
  output EQ
);

  wire comparador4bits_1_bt, comparador4bits_1_eq, comparador4bits_1_lw;

  comparador4bits comparador4bits_1 (
    .r_BT(1'b0), .r_LW(1'b0), .r_EQ(1'b0), .B3(B7), .A3(A7), .B2(B6), .A2(A6), .B1(B5), .A1(A5), .B0(B4),
    .A0(A4), .BT(comparador4bits_1_bt), .LW(comparador4bits_1_lw), .EQ(comparador4bits_1_eq));
  comparador4bits comparador4bits_2 (
    .r_BT(comparador4bits_1_bt), .r_LW(comparador4bits_1_lw), .r_EQ(comparador4bits_1_eq), .B3(B3), .A3(A3),
    .B2(B2), .A2(A2), .B1(B1), .A1(A1), .B0(B0), .A0(A0), .BT(BT), .LW(LW), .EQ(EQ));
endmodule

module comparadorbasico1bit (
  input  in_1,
  input  in_2,
  output better,
  output lower,
  output equal
);

  wire xor_1_out;

  xor xor_1 (xor_1_out, in_1, in_2);
  and and_1 (equal, in_1, in_2);
  and and_2 (better, in_1, xor_1_out);
  and and_3 (lower, in_2, xor_1_out);
endmodule

module comparador4bits (
  input  r_BT,
  input  r_LW,
  input  r_EQ,
  input  B3,
  input  A3,
  input  B2,
  input  A2,
  input  B1,
  input  A1,
  input  B0,
  input  A0,
  output BT,
  output LW,
  output EQ
);

  wire comparador1bit_1_bt, comparador1bit_1_eq, comparador1bit_1_lw, comparador1bit_2_bt,
       comparador1bit_2_eq, comparador1bit_2_lw, comparador1bit_3_bt, comparador1bit_3_eq,
       comparador1bit_3_lw;

  comparador1bit comparador1bit_1 (
    .B0(B3), .A0(A3), .r_BT(r_BT), .r_LW(r_LW), .r_EQ(r_EQ), .BT(comparador1bit_1_bt),
    .LW(comparador1bit_1_lw), .EQ(comparador1bit_1_eq));
  comparador1bit comparador1bit_2 (
    .B0(B2), .A0(A2), .r_BT(comparador1bit_1_bt), .r_LW(comparador1bit_1_lw), .r_EQ(comparador1bit_1_eq),
    .BT(comparador1bit_2_bt), .LW(comparador1bit_2_lw), .EQ(comparador1bit_2_eq));
  comparador1bit comparador1bit_3 (
    .B0(B1), .A0(A1), .r_BT(comparador1bit_2_bt), .r_LW(comparador1bit_2_lw), .r_EQ(comparador1bit_2_eq),
    .BT(comparador1bit_3_bt), .LW(comparador1bit_3_lw), .EQ(comparador1bit_3_eq));
  comparador1bit comparador1bit_4 (
    .B0(B0), .A0(A0), .r_BT(comparador1bit_3_bt), .r_LW(comparador1bit_3_lw), .r_EQ(comparador1bit_3_eq),
    .BT(BT), .LW(LW), .EQ(EQ));
endmodule

module multiplicador8bits (
  input  A3,
  input  A2,
  input  A1,
  input  A0,
  input  B3,
  input  B2,
  input  B1,
  input  B0,
  output S7,
  output S6,
  output S5,
  output S4,
  output S3,
  output S2,
  output S1,
  output S0
);

  wire and_1_out, and_2_out, and_3_out, and_4_out, and_5_out, and_6_out, and_7_out, and_8_out, and_9_out,
       and_10_out, and_11_out, and_12_out, and_13_out, and_14_out, and_15_out, somador4bits_2_c1,
       somador4bits_2_c2, somador4bits_2_c3, somador4bits_2_cout, somador4bits_3_c1, somador4bits_3_c2,
       somador4bits_3_c3, somador4bits_3_cout;

  and and_1 (and_1_out, B3, A3);
  and and_2 (and_2_out, B3, A2);
  and and_3 (and_3_out, B3, A1);
  and and_4 (and_4_out, B3, A0);
  and and_5 (and_5_out, B2, A3);
  and and_6 (and_6_out, B2, A2);
  and and_7 (and_7_out, B2, A1);
  and and_8 (and_8_out, B2, A0);
  somador4bits somador4bits_1 (
    .B3(somador4bits_2_cout), .A3(and_1_out), .B2(somador4bits_2_c3), .A2(and_2_out), .B1(somador4bits_2_c2),
    .A1(and_3_out), .B0(somador4bits_2_c1), .A0(and_4_out), .C3(S6), .C2(S5), .C1(S4), .C0(S3), .cout(S7));  // open: CARRY
  and and_9 (and_9_out, B1, A3);
  and and_10 (and_10_out, B1, A2);
  and and_11 (and_11_out, B1, A1);
  and and_12 (and_12_out, B1, A0);
  somador4bits somador4bits_2 (
    .B3(somador4bits_3_cout), .A3(and_5_out), .B2(somador4bits_3_c3), .A2(and_6_out), .B1(somador4bits_3_c2),
    .A1(and_7_out), .B0(somador4bits_3_c1), .A0(and_8_out), .C3(somador4bits_2_c3), .C2(somador4bits_2_c2),
    .C1(somador4bits_2_c1), .C0(S2), .cout(somador4bits_2_cout));  // open: CARRY
  and and_13 (and_13_out, B0, A3);
  and and_14 (and_14_out, B0, A2);
  and and_15 (and_15_out, B0, A1);
  somador4bits somador4bits_3 (
    .CARRY(1'b0), .B3(1'b0), .A3(and_9_out), .B2(and_13_out), .A2(and_10_out), .B1(and_14_out),
    .A1(and_11_out), .B0(and_15_out), .A0(and_12_out), .C3(somador4bits_3_c3), .C2(somador4bits_3_c2),
    .C1(somador4bits_3_c1), .C0(S1), .cout(somador4bits_3_cout));
  and and_16 (S0, B0, A0);
endmodule
